# Fritzing sketch Schematic (saved by Fritzing 0.9.9b)
perfboards: 2

parts:
  Part1 = InvenSense MPU6050  # not connected
  J1 = male pin header, 8 pins [form="♂ (male)"]
  J2 = male pin header, 8 pins [form="♂ (male)"]
  J3 = male pin header, 8 pins [form="♂ (male)"]
  WeMos_D1_Mini1 = WeMos D1 Mini  # not connected

nets:
  N1: J1.pin2, J3.pin2
  N2: J1.pin5, J3.pin4
  N3: J1.pin6, J3.pin3
  N4: J2.pin1, J3.pin1

notes:
  Top
  Bottom
